# Fritzing sketch sketch (saved by Fritzing 0.9.3b)
breadboards: 1

parts:
  R5 = Basic Flex Resistor
  Part1 = Arduino Nano (Rev3.0)
  R7 = Resistor [tolerance=±5% resistance=47k package="0603 [SMD]"]
  R8 = Basic Flex Resistor
  R9 = Resistor [tolerance=±5% resistance=47k package="0603 [SMD]"]
  R10 = Basic Flex Resistor
  R11 = Resistor [tolerance=±5% resistance=47k package="0603 [SMD]"]
  R12 = Basic Flex Resistor
  R13 = Resistor [tolerance=±5% resistance=47k package="0603 [SMD]"]
  R14 = Basic Flex Resistor
  R15 = Resistor [tolerance=±5% resistance=47k package="0603 [SMD]"]
  R16 = Basic Flex Resistor
  R17 = Resistor [tolerance=±5% resistance=47k package="0603 [SMD]"]
  U1 = 74HC4051 [package=so16]
  Part2 = NRF24L01+ Breakout Board  # not connected

nets:
  N1: R5.Pin_2, R7.Pin_0, U1.IO3
  N2: R5.pin_1, Part1.VIN, R8.pin_1, R10.pin_1, R12.pin_1, R14.pin_1, R16.pin_1
  GND: Part1.GND, R7.Pin_1, R9.Pin_1, R11.Pin_1, R17.Pin_1, U1.VSS
  N3: Part1.D2, U1.A
  N4: Part1.D3, U1.B
  N5: Part1.D4, U1.C
  5V: Part1.5V, U1.VDD
  N6: Part1.A7, U1.IO
  N7: R8.Pin_2, R9.Pin_0, U1.IO0
  N8: R10.Pin_2, R11.Pin_0, U1.IO1
  N9: R12.Pin_2, R13.Pin_0, U1.IO2
  N10: R14.Pin_2, R15.Pin_0, U1.IO6
  N11: R16.Pin_2, R17.Pin_0, U1.IO4

notes:
  Nano pins:
  D2,D3,D3 - mux select
  A7 - mux input (flex)
